# Fritzing sketch miniboard (saved by Fritzing 0.9.3b)
circuit board: 8.46667cm x 5.64444cm

parts:
  IC1 = MICROCONTROLLER [package=dil28-3-simon-kit]
  XTAL1 = CRYSTAL - kHz [frequency="16 MHz"]
  C1 = Ceramic Capacitor [capacitance=22pF package="100 mil [THT, multilayer]"]
  C2 = Ceramic Capacitor [capacitance=22pF package="100 mil [THT, multilayer]"]
  R1 = Resistor [tolerance=±5% resistance=10k package=THT]
  S2 = Toggle Switch [package=THT]
  IC2 = Voltage Regulator [package=to-220-alt]
  D1 = Diode [package=diode-hv]
  J1 = female pin header, 2 pins [form="♀ (female)"]
  S3 = Pushbutton [package="[SMD]"]

nets:
  N1: IC1.PC6(_RESET), IC1.VCC, IC1.AVCC, IC1.AREF, R1.Pin_1, IC2.OUT
  GND: IC1.GND, IC1.AGND, C1.1, C2.1, IC2.GND, J1.pin1, S3.Pin_1, S3.Pin_2
  N2: IC1.PB6(XTAL1_TOSC1), XTAL1.pin_0, C1.0
  N3: IC1.PB7(XTAL2_TOSC2), XTAL1.pin_1, C2.0
  N4: R1.Pin_0, S3.Pin_3, S3.Pin_4
  N5: S2.L2, D1.A
  N6: IC2.IN, D1.C
